# Fritzing sketch projeto (saved by Fritzing 0.9.2b)
breadboards: 1

parts:
  S1 = Pushbutton [package="[THT]"]
  S2 = Pushbutton [package="[THT]"]
  Componente1 = Arduino Uno (Rev3)  # not connected
  J1 = Piezo Speaker  # not connected
  J2 = Piezo Speaker  # not connected
  LED1 = LED - 5mm [color="Red (633nm)" package="5 mm [THT]"]  # not connected
  LED2 = LED - 5mm [color="Red (633nm)" package="5 mm [THT]"]  # not connected

nets:
  N1: S1.Pin_1, S1.Pin_2
  N2: S1.Pin_3, S1.Pin_4
  N3: S2.Pin_1, S2.Pin_2
  N4: S2.Pin_3, S2.Pin_4
